// Logisim project parker.circ as structural Verilog: 4 circuits, main circuit bonus
module main (
);

  wire clock_1_out, dec_7seg_driver_1_a_2, dec_7seg_driver_1_b_2, dec_7seg_driver_1_c_2,
       dec_7seg_driver_1_d_2, dec_7seg_driver_1_e, dec_7seg_driver_1_f, dec_7seg_driver_1_g,
       dec_counter_1__0, dec_counter_1__1, dec_counter_1__2, dec_counter_1__3;

  _7_Segment_Display u_7_segment_display_1 ();  // open: g, f, a, b, e, d, c, dp
  Clock clock_1 (.out(clock_1_out));
  dec_counter dec_counter_1 (
    .Clock(clock_1_out), ._0(dec_counter_1__0), ._1(dec_counter_1__1), ._2(dec_counter_1__2),
    ._3(dec_counter_1__3));  // open: RESET
  dec_7seg_driver dec_7seg_driver_1 (
    .D(dec_counter_1__0), .C(dec_counter_1__1), .B(dec_counter_1__2), .A(dec_counter_1__3),
    .a_2(dec_7seg_driver_1_a_2), .b_2(dec_7seg_driver_1_b_2), .c_2(dec_7seg_driver_1_c_2),
    .d_2(dec_7seg_driver_1_d_2), .e(dec_7seg_driver_1_e), .f(dec_7seg_driver_1_f), .g(dec_7seg_driver_1_g));
  _7_Segment_Display u_7_segment_display_2 (
    .g(dec_7seg_driver_1_g), .f(dec_7seg_driver_1_f), .a(dec_7seg_driver_1_a_2), .b(dec_7seg_driver_1_b_2),
    .e(dec_7seg_driver_1_e), .d(dec_7seg_driver_1_d_2), .c(dec_7seg_driver_1_c_2));  // open: dp

  // Notes on the sheet:
  //   a
  //   g
  //   f
  //   e
  //   d
  //   b
  //   c
endmodule

module bonus (
);

  wire clock_1_out, dec_7seg_driver_1_a_2, dec_7seg_driver_1_b_2, dec_7seg_driver_1_c_2,
       dec_7seg_driver_1_d_2, dec_7seg_driver_1_e, dec_7seg_driver_1_f, dec_7seg_driver_1_g,
       dec_7seg_driver_2_a_2, dec_7seg_driver_2_b_2, dec_7seg_driver_2_c_2, dec_7seg_driver_2_d_2,
       dec_7seg_driver_2_e, dec_7seg_driver_2_f, dec_7seg_driver_2_g, dec_counter_1__0, dec_counter_1__1,
       dec_counter_1__2, dec_counter_1__3, dec_counter_1_reset, dec_counter_2__0, dec_counter_2__1,
       dec_counter_2__2, dec_counter_2__3;

  _7_Segment_Display u_7_segment_display_1 ();  // open: g, f, a, b, e, d, c, dp
  Clock clock_1 (.out(clock_1_out));
  dec_counter dec_counter_1 (
    .Clock(clock_1_out), .RESET(dec_counter_1_reset), ._0(dec_counter_1__0), ._1(dec_counter_1__1),
    ._2(dec_counter_1__2), ._3(dec_counter_1__3));
  dec_counter dec_counter_2 (
    .Clock(dec_counter_1_reset), ._0(dec_counter_2__0), ._1(dec_counter_2__1), ._2(dec_counter_2__2),
    ._3(dec_counter_2__3));  // open: RESET
  dec_7seg_driver dec_7seg_driver_1 (
    .D(dec_counter_1__0), .C(dec_counter_1__1), .B(dec_counter_1__2), .A(dec_counter_1__3),
    .a_2(dec_7seg_driver_1_a_2), .b_2(dec_7seg_driver_1_b_2), .c_2(dec_7seg_driver_1_c_2),
    .d_2(dec_7seg_driver_1_d_2), .e(dec_7seg_driver_1_e), .f(dec_7seg_driver_1_f), .g(dec_7seg_driver_1_g));
  dec_7seg_driver dec_7seg_driver_2 (
    .D(dec_counter_2__0), .C(dec_counter_2__1), .B(dec_counter_2__2), .A(dec_counter_2__3),
    .a_2(dec_7seg_driver_2_a_2), .b_2(dec_7seg_driver_2_b_2), .c_2(dec_7seg_driver_2_c_2),
    .d_2(dec_7seg_driver_2_d_2), .e(dec_7seg_driver_2_e), .f(dec_7seg_driver_2_f), .g(dec_7seg_driver_2_g));
  _7_Segment_Display u_7_segment_display_2 (
    .g(dec_7seg_driver_2_g), .f(dec_7seg_driver_2_f), .a(dec_7seg_driver_2_a_2), .b(dec_7seg_driver_2_b_2),
    .e(dec_7seg_driver_2_e), .d(dec_7seg_driver_2_d_2), .c(dec_7seg_driver_2_c_2));  // open: dp
  _7_Segment_Display u_7_segment_display_3 (
    .g(dec_7seg_driver_1_g), .f(dec_7seg_driver_1_f), .a(dec_7seg_driver_1_a_2), .b(dec_7seg_driver_1_b_2),
    .e(dec_7seg_driver_1_e), .d(dec_7seg_driver_1_d_2), .c(dec_7seg_driver_1_c_2));  // open: dp

  // Notes on the sheet:
  //   a
  //   b
  //   g
  //   f
  //   e
  //   c
  //   d
endmodule

module dec_7seg_driver (
  input  D,
  input  C,
  input  B,
  input  A,
  output a_2,
  output b_2,
  output c_2,
  output d_2,
  output e,
  output f,
  output g
);

  wire and_1_out, and_2_out, and_3_out, and_4_out, and_5_out, and_6_out, and_7_out, and_8_out, and_9_out,
       and_10_out, and_11_out, and_12_out, and_13_out, and_14_out, and_15_out, and_16_out, not_1_out,
       not_2_out, not_3_out, not_4_out;

  not not_1 (not_1_out, D);
  not not_2 (not_2_out, C);
  not not_3 (not_3_out, B);
  not not_4 (not_4_out, A);
  and and_1 (and_1_out, not_1_out, not_3_out);
  and and_2 (and_2_out, D, B);
  and and_3 (and_3_out, not_1_out, not_2_out);
  and and_4 (and_4_out, D, C);
  and and_5 (and_5_out, not_1_out, not_3_out);
  and and_6 (and_6_out, not_1_out, C);
  and and_7 (and_7_out, C, not_3_out);
  and and_8 (and_8_out, D, not_2_out, B);
  and and_9 (and_9_out, not_1_out, not_3_out);
  and and_10 (and_10_out, not_1_out, C);
  and and_11 (and_11_out, not_1_out, not_2_out);
  and and_12 (and_12_out, not_1_out, B);
  and and_13 (and_13_out, not_2_out, B);
  and and_14 (and_14_out, not_2_out, B);
  and and_15 (and_15_out, not_1_out, C);
  and and_16 (and_16_out, C, not_3_out);
  or or_1 (a_2, and_1_out, A, C, and_2_out);
  or or_2 (b_2, and_3_out, not_3_out, and_4_out);
  or or_3 (c_2, not_2_out, B, D);
  or or_4 (d_2, and_5_out, and_6_out, A, and_7_out, and_8_out);
  or or_5 (e, and_9_out, and_10_out);
  or or_6 (f, and_11_out, and_12_out, A, and_13_out);
  or or_7 (g, A, and_14_out, and_15_out, and_16_out);
endmodule

module dec_counter (
  input  Clock,
  output _0,
  output _1,
  output _2,
  output _3,
  output RESET
);

  wire and_2_out, and_3_out, and_4_out, and_5_out, and_6_out, and_7_out, and_8_out, D1_qn, D2_qn, D3_qn,
       D4_qn, or_1_out, or_2_out, or_3_out;

  and and_1 (RESET, _3, D2_qn, D3_qn, _0);
  and and_2 (and_2_out, _3, D4_qn);
  and and_3 (and_3_out, _2, _1, _0);
  and and_4 (and_4_out, _2, D3_qn);
  and and_5 (and_5_out, _2, D4_qn);
  and and_6 (and_6_out, D2_qn, _1, _0);
  and and_7 (and_7_out, _1, D4_qn);
  and and_8 (and_8_out, D1_qn, D3_qn, _0);
  or or_1 (or_1_out, and_2_out, and_3_out);
  or or_2 (or_2_out, and_4_out, and_5_out, and_6_out);
  or or_3 (or_3_out, and_7_out, and_8_out);
  D_Flip_Flop #(.trigger("falling")) D1 (.clk(Clock), .D(or_1_out), .Q(_3), .Qn(D1_qn));  // open: preset, en, reset
  D_Flip_Flop #(.trigger("falling")) D2 (.clk(Clock), .D(or_2_out), .Q(_2), .Qn(D2_qn));  // open: preset, en, reset
  D_Flip_Flop #(.trigger("falling")) D3 (.clk(Clock), .D(or_3_out), .Q(_1), .Qn(D3_qn));  // open: preset, en, reset
  D_Flip_Flop #(.trigger("falling")) D4 (.clk(Clock), .D(D4_qn), .Q(_0), .Qn(D4_qn));  // open: preset, en, reset
endmodule
